// Digital circuit BancoDeRegistradores.dig as structural Verilog
module BancoDeRegistradores (
);

  wire [7:0] register_1_q, register_2_q, register_3_q, register_4_q, register_5_q, register_6_q,
       register_7_q, register_8_q;

  Register #(.Bits(8)) register_1 (.Q(register_1_q));  // open: D, C, en
  Register register_2 (.Q(register_2_q[0]));  // open: D, C, en
  Register register_3 (.Q(register_3_q[0]));  // open: D, C, en
  Register register_4 (.Q(register_4_q[0]));  // open: D, C, en
  Register register_5 (.Q(register_5_q[0]));  // open: D, C, en
  Register register_6 (.Q(register_6_q[0]));  // open: D, C, en
  Register register_7 (.Q(register_7_q[0]));  // open: D, C, en
  Register register_8 (.Q(register_8_q[0]));  // open: D, C, en
  Multiplexer #(.Bits(8), .Selector_Bits(3)) multiplexer_1 (
    .in_0(register_1_q), .in_1(register_2_q), .in_2(register_3_q), .in_3(register_4_q), .in_4(register_5_q),
    .in_5(register_6_q), .in_6(register_7_q), .in_7(register_8_q));  // open: sel, out
  // Pins of 1 and 8 bits meet at register_2_q
  // Pins of 1 and 8 bits meet at register_3_q
  // Pins of 1 and 8 bits meet at register_4_q
  // Pins of 1 and 8 bits meet at register_5_q
  // Pins of 1 and 8 bits meet at register_6_q
  // Pins of 1 and 8 bits meet at register_7_q
  // Pins of 1 and 8 bits meet at register_8_q
endmodule
